# Fritzing sketch Esquema eletrico - fritzing (saved by Fritzing 1.0.5)
breadboards: 1

parts:
  A1 = ESP32 DevKitc V4
  DHT1 = DHT22 Humidity and Temperature Sensor
  Componente1 = BH1750FVI Breakout Board [part_number=BH1750FVI]
  M1 = DFR sen0308 [package=THT]

nets:
  VDD: A1.Pin_1, DHT1.VDD, Componente1.VCC, M1.pin4
  N1: A1.Pin_5, M1.pin2
  N2: A1.Pin_13, DHT1.DATA
  GND: A1.Pin_14, A1.Pin_32, A1.Pin_38, DHT1.GND, Componente1.GND, M1.pin1, M1.pin3
  N3: A1.Pin_33, Componente1.SDA
  N4: A1.Pin_36, Componente1.SCL

custom parts:
  ESP32 DevKitc V4: ESP32-DevKitC board with ESP32-WROOM-32 module. ESP32-DevKitC V4 is a small-sized ESP32-based development board produced by Espressif. Most of the pins on the ESP module are broken out to the pin headers on the board. The pins D0, D1, D2, D3, CMD and CLK are used internally for communication between ESP32 and SPI flash memory. They are grouped on both sides near the USB connector. Avoid using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
  BH1750FVI Breakout Board: The ROHM Semiconductor BH1750FVI is a digital ambient light sensor for the I2C bus interface. The BH750FVI is able to detect a wide range of light intensities (1-65535 lux). The spectral range is similar to that of the human eye.
  DFR sen0308: This is a new type of waterproof soil moisture sensor introduced by DFRobot. Compared with the previous version of the soil moisture sensor, it has increased waterproof performance, optimized corrosion resistance, increased plate length and optimized circuit performance. Compared with the resistive sensor, the capacitive soil moisture sensor solves the problem that the resistive sensor is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
